# Fritzing sketch final-diagram_CART360 (saved by Fritzing 1.0.6)
breadboards: 1

parts:
  Mod1 = Raspberry Pi Pico W
  LED1 = smd LED [color="Green (555nm)" package="0805 [SMD]"]
  R2 = Resistor [tolerance=±5% resistance=220 package="2512 [SMD]"]
  LED2 = smd LED [color="Yellow (585nm)" package="0805 [SMD]"]
  R3 = Resistor [tolerance=±5% resistance=220 package="2512 [SMD]"]
  LED3 = smd LED [color="Red (633nm)" package="0805 [SMD]"]
  Composant1 = LCD1602-I2C
  FC-1 = Sound Sensor
  R4 = Resistor [tolerance=±5% resistance=220 package="2512 [SMD]"]

nets:
  N1: Mod1.pin_1, FC-1.OUT
  N2: Mod1.pin_3, Mod1.pin_8, Mod1.pin_13, Mod1.pin_18, Mod1.pin_23, Mod1.pin_28, Mod1.pin_33, Mod1.pin_38, Composant1.GND
  N3: Mod1.pin_11, Composant1.SDA
  N4: Mod1.pin_12, Composant1.SCL
  N5: Mod1.pin_21, R4.Pin_0
  N6: Mod1.pin_22, R2.Pin_0
  N7: Mod1.pin_24, R3.Pin_0
  N8: Mod1.pin_40, Composant1.VCC
  N9: LED1.cathode, LED2.cathode, LED3.cathode
  N10: LED1.anode, R4.Pin_1
  N11: R2.Pin_1, LED2.anode
  N12: R3.Pin_1, LED3.anode

custom parts:
  Raspberry Pi Pico W: Raspberry Pi Pico W. Based around the RP2040 microcontroller the Pico W is a low cost microcontroller device bringing Raspberry Pi quality, cost, and easy of use to the microcontroller space. The areas marked KEEPOUT in pcb silkscreen should not have traces running through them to avoid shorts on a soldered in module!
  LCD1602-I2C: A standard character display, usually with 2x16 characters. Comes in many colors with LCM1602 IIC attached.
